// Logisim project input.circ as structural Verilog: 5 circuits, main circuit main
// Runway Status
module main (
  input  in_1,
  input  in_2,
  input  in_3
);

  wire clock_1_out, Runway_Picker_en_2, Runway_Picker_o1, Runway_Picker_o2, Runway_Picker_o3,
       Runway_Picker_o4, Runway_status_runway_a_feedback, Runway_status_runway_a_status,
       Runway_status_runway_b_feedback, Runway_status_runway_b_status, Runway_status_wait_signal;

  runway_picker Runway_Picker (
    .B(Runway_status_runway_b_feedback), .A(Runway_status_runway_a_feedback), .En(in_3), .D2(in_2),
    .D1(in_1), .En_2(Runway_Picker_en_2), .O4(Runway_Picker_o4), .O3(Runway_Picker_o3),
    .O2(Runway_Picker_o2), .O1(Runway_Picker_o1));
  runway_status Runway_status (
    .I3(Runway_Picker_o1), .I2(Runway_Picker_o2), .I1(Runway_Picker_o3), .I0(Runway_Picker_o4),
    .En(Runway_Picker_en_2), .Clock(clock_1_out), .Runway_B_Feedback(Runway_status_runway_b_feedback),
    .Runway_A_Feedback(Runway_status_runway_a_feedback), .Runway_B_Status(Runway_status_runway_b_status),
    .Runway_A_Status(Runway_status_runway_a_status), .Wait_Signal(Runway_status_wait_signal));
  Clock clock_1 (.out(clock_1_out));
  LED led_1 (.in(Runway_status_wait_signal));
  LED led_2 (.in(Runway_status_wait_signal));
  LED Wait_For_Landing (.in(Runway_status_wait_signal));
  LED led_3 (.in(Runway_status_runway_b_status));
  LED led_4 (.in(Runway_status_runway_a_status));
  LED led_5 (.in(Runway_status_runway_a_status));
  LED led_6 (.in(Runway_status_runway_a_status));
  LED led_7 (.in(Runway_status_runway_a_status));
  LED led_8 (.in(Runway_status_runway_a_status));
  LED led_9 (.in(Runway_status_runway_a_status));
  LED led_10 (.in(Runway_status_runway_a_status));
  LED led_11 (.in(Runway_status_runway_b_status));
  LED led_12 (.in(Runway_status_wait_signal));
  LED led_13 (.in(Runway_status_wait_signal));
  LED Wait_For_Landing_2 (.in(Runway_status_wait_signal));
  LED led_14 (.in(Runway_status_runway_b_status));
  LED led_15 (.in(Runway_status_runway_b_status));
  LED led_16 (.in(Runway_status_runway_b_status));
  LED led_17 (.in(Runway_status_runway_b_status));
  LED led_18 (.in(Runway_status_runway_b_status));

  // Notes on the sheet:
  //   Runway B
  //   Runway A
endmodule

module runway_picker (
  input  B,
  input  A,
  input  En,
  input  D2,
  input  D1,
  output En_2,
  output O4,
  output O3,
  output O2,
  output O1
);

  wire and_1_out, and_2_out, not_1_out, not_2_out, not_3_out, or_1_out;

  and and_1 (and_1_out, B, A);
  not not_1 (not_1_out, B);
  not not_2 (not_2_out, D2);
  and and_2 (and_2_out, not_1_out, not_2_out);
  not not_3 (not_3_out, and_1_out);
  or or_1 (or_1_out, A, and_2_out);
  and and_3 (O4, En, 1'b1);
  and and_4 (O3, En, and_1_out);
  and and_5 (O2, En, not_3_out);
  and and_6 (O1, En, or_1_out);

  assign En_2 = En;

  // Notes on the sheet:
  //   Runway Picker
  //   O4 = 1
  //   O3 = A.B
  //   O2 = (A.B)'
  //   O1 = A + B'.D2'
endmodule

module runway_status (
  input  I3,
  input  I2,
  input  I1,
  input  I0,
  input  En,
  input  Clock,
  output Runway_B_Feedback,
  output Runway_A_Feedback,
  output Runway_B_Status,
  output Runway_A_Status,
  output Wait_Signal
);

  wire _4_16_Decoder__10, _4_16_Decoder__11, Counter_2_carry_is_1_when_counter_finishes,
       Counter_carry_is_1_when_counter_finishes, not_1_out, not_2_out, not_3_out, not_4_out, s_r_ff_1_q,
       s_r_ff_2_q;

  decoder _4_16_Decoder (
    .A__LSB(I3), .B(I2), .C(I1), .D__MSB(I0), .Enable(En), ._10(_4_16_Decoder__10), ._11(_4_16_Decoder__11),
    ._13(Wait_Signal));  // open: _0, _1, _2, _3, _4, _5, _6, _7, _8, _9, _12, _14, _15
  S_R_Flip_Flop s_r_ff_1 (
    .S(_4_16_Decoder__10), .clk(Clock), .R(1'b0), .Q(s_r_ff_1_q),
    .reset(Counter_carry_is_1_when_counter_finishes));  // open: Qn, preset, en
  counter Counter (
    .Carry_is_1_when_counter_finishes(Counter_carry_is_1_when_counter_finishes), .Clock(Clock),
    .Reset(not_1_out));
  not not_1 (not_1_out, s_r_ff_1_q);
  not not_2 (not_2_out, Counter_carry_is_1_when_counter_finishes);
  counter Counter_2 (
    .Carry_is_1_when_counter_finishes(Counter_2_carry_is_1_when_counter_finishes), .Clock(Clock),
    .Reset(not_4_out));
  D_Flip_Flop d_ff_1 (.clk(En), .D(Runway_B_Status), .Q(Runway_B_Feedback));  // open: Qn, preset, en, reset
  D_Flip_Flop d_ff_2 (.clk(En), .D(Runway_A_Status), .Q(Runway_A_Feedback));  // open: Qn, preset, en, reset
  not not_3 (not_3_out, Counter_2_carry_is_1_when_counter_finishes);
  S_R_Flip_Flop s_r_ff_2 (
    .S(_4_16_Decoder__11), .clk(Clock), .R(1'b0), .Q(s_r_ff_2_q),
    .reset(Counter_2_carry_is_1_when_counter_finishes));  // open: Qn, preset, en
  not not_4 (not_4_out, s_r_ff_2_q);
  and and_1 (Runway_B_Status, s_r_ff_2_q, not_3_out);
  and and_2 (Runway_A_Status, s_r_ff_1_q, not_2_out);

  // Notes on the sheet:
  //   a
  //   b
  //   d
endmodule

module decoder (
  input  A__LSB,
  input  B,
  input  C,
  input  D__MSB,
  input  Enable,
  output _0,
  output _1,
  output _2,
  output _3,
  output _4,
  output _5,
  output _6,
  output _7,
  output _8,
  output _9,
  output _10,
  output _11,
  output _12,
  output _13,
  output _14,
  output _15
);

  wire not_1_out, not_2_out, not_3_out, not_4_out;

  not not_1 (not_1_out, A__LSB);
  not not_2 (not_2_out, B);
  not not_3 (not_3_out, C);
  not not_4 (not_4_out, D__MSB);
  and and_1 (_0, Enable, not_4_out, not_3_out, not_2_out, not_1_out);
  and and_2 (_1, Enable, not_4_out, not_3_out, not_2_out, A__LSB);
  and and_3 (_3, Enable, not_4_out, not_3_out, B, A__LSB);
  and and_4 (_2, Enable, not_4_out, not_3_out, B, not_1_out);
  and and_5 (_4, Enable, not_4_out, C, not_2_out, not_1_out);
  and and_6 (_5, Enable, not_4_out, C, not_2_out, A__LSB);
  and and_7 (_6, Enable, not_4_out, C, B, not_1_out);
  and and_8 (_7, Enable, not_4_out, C, B, A__LSB);
  and and_9 (_8, Enable, D__MSB, not_3_out, not_2_out, not_1_out);
  and and_10 (_9, Enable, D__MSB, not_3_out, not_2_out, A__LSB);
  and and_11 (_11, Enable, D__MSB, not_3_out, B, A__LSB);
  and and_12 (_10, Enable, D__MSB, not_3_out, B, not_1_out);
  and and_13 (_12, Enable, D__MSB, C, not_2_out, not_1_out);
  and and_14 (_14, Enable, D__MSB, C, B, not_1_out);
  and and_15 (_13, Enable, D__MSB, C, not_2_out, A__LSB);
  and and_16 (_15, Enable, D__MSB, C, B, A__LSB);

  // Notes on the sheet:
  //   4:16 Decoder
endmodule

module counter (
  input  Clock,
  input  Reset,
  output Carry_is_1_when_counter_finishes
);

  wire and_1_out, not_1_out;
  wire [3:0] t_ff_1_q;

  and and_1 (and_1_out, not_1_out, Clock);
  not not_1 (not_1_out, Carry_is_1_when_counter_finishes);
  T_Flip_Flop t_ff_1 (.clk(and_1_out), .T(1'b1), .Q(t_ff_1_q[0]), .reset(Reset), .en(1'b1));  // open: Qn, preset
  and and_2 (Carry_is_1_when_counter_finishes, t_ff_1_q[3], t_ff_1_q[2]);
  T_Flip_Flop #(.trigger("falling")) t_ff_2 (
    .clk(t_ff_1_q[0]), .T(1'b1), .Q(t_ff_1_q[1]), .reset(Reset), .en(1'b1));  // open: Qn, preset
  T_Flip_Flop #(.trigger("falling")) t_ff_3 (
    .clk(t_ff_1_q[1]), .T(1'b1), .Q(t_ff_1_q[2]), .reset(Reset), .en(1'b1));  // open: Qn, preset
  // Probe on t_ff_1_q
  T_Flip_Flop #(.trigger("falling")) t_ff_4 (
    .clk(t_ff_1_q[2]), .T(1'b1), .Q(t_ff_1_q[3]), .reset(Reset), .en(1'b1));  // open: Qn, preset

  // Notes on the sheet:
  //   4 bit up counter
endmodule
