// Logisim project runway_picker.circ as structural Verilog: 1 circuit, main circuit main
module main (
  input  [3:0] D1D2AB,
  output [3:0] O4O3O2O1
);

  wire and_2_out, not_1_out, not_2_out;

  and and_1 (O4O3O2O1[2], D1D2AB[0], D1D2AB[1]);
  not not_1 (not_1_out, D1D2AB[0]);
  not not_2 (not_2_out, D1D2AB[2]);
  and and_2 (and_2_out, not_1_out, not_2_out);
  not not_3 (O4O3O2O1[1], O4O3O2O1[2]);
  or or_1 (O4O3O2O1[0], D1D2AB[1], and_2_out);

  assign O4O3O2O1[3] = 1'b1;

  // Notes on the sheet:
  //   Runway Picker
  //   O4 = 1
  //   O3 = A.B
  //   O2 = (A.B)'
  //   O1 = A + B'.D2'
endmodule
