// Logisim project runway_status.circ as structural Verilog: 1 circuit, main circuit main
module main (
  input  [4:0] Bit_0_is_enable,
  output Runway_B_Status,
  output Runway_A_Status,
  output Wait_signal
);

  wire clock_1_out, clock_2_out, counter_1_carry, counter_2_carry, demultiplexer_1_out10,
       demultiplexer_1_out11, not_1_out, not_2_out, not_3_out, not_4_out, s_r_ff_1_q, s_r_ff_2_q;

  Demultiplexer #(.select(4)) demultiplexer_1 (
    .out10(demultiplexer_1_out10), .out11(demultiplexer_1_out11), .out13(Wait_signal),
    .in(Bit_0_is_enable[0]), .sel(Bit_0_is_enable[4:1]));  // open: out0, out1, out2, out3, out4, out5, out6, out7, out8, out9, out12, out14, out15, en
  Clock clock_1 (.out(clock_1_out));
  and and_1 (Runway_A_Status, not_1_out, s_r_ff_1_q);
  not not_1 (not_1_out, counter_1_carry);
  S_R_Flip_Flop s_r_ff_1 (
    .S(demultiplexer_1_out10), .clk(clock_1_out), .R(1'b0), .Q(s_r_ff_1_q), .reset(counter_1_carry));  // open: Qn, preset, en
  Counter #(.width(4), .max('hd), .ongoal("stay")) counter_1 (
    .carry(counter_1_carry), .clk(clock_1_out), .clr(not_2_out));  // open: load, D, count, Q
  not not_2 (not_2_out, s_r_ff_1_q);
  Clock clock_2 (.out(clock_2_out));
  and and_2 (Runway_B_Status, not_4_out, s_r_ff_2_q);
  S_R_Flip_Flop s_r_ff_2 (
    .S(demultiplexer_1_out11), .clk(clock_2_out), .R(1'b0), .Q(s_r_ff_2_q), .reset(counter_2_carry));  // open: Qn, preset, en
  Counter #(.width(4), .max('hd), .ongoal("stay")) counter_2 (
    .carry(counter_2_carry), .clk(clock_2_out), .clr(not_3_out));  // open: load, D, count, Q
  not not_3 (not_3_out, s_r_ff_2_q);
  not not_4 (not_4_out, counter_2_carry);

  // Notes on the sheet:
  //   Bit 1-4 is the output from runway picker
  //   a
  //   b
  //   d
endmodule
