// Logisim project counter.circ as structural Verilog: 1 circuit, main circuit main
module main (
  input  Reset,
  input  Enable
);

  wire and_1_out, and_2_out, clock_1_out, not_1_out;
  wire [3:0] t_ff_1_q;

  Clock clock_1 (.out(clock_1_out));
  and and_1 (and_1_out, not_1_out, clock_1_out);
  not not_1 (not_1_out, and_2_out);
  T_Flip_Flop t_ff_1 (.clk(and_1_out), .T(1'b1), .Q(t_ff_1_q[0]), .reset(Reset), .en(Enable));  // open: Qn, preset
  and and_2 (and_2_out, t_ff_1_q[3], t_ff_1_q[2], t_ff_1_q[1]);
  T_Flip_Flop #(.trigger("falling")) t_ff_2 (
    .clk(t_ff_1_q[0]), .T(1'b1), .Q(t_ff_1_q[1]), .reset(Reset), .en(Enable));  // open: Qn, preset
  T_Flip_Flop #(.trigger("falling")) t_ff_3 (
    .clk(t_ff_1_q[1]), .T(1'b1), .Q(t_ff_1_q[2]), .reset(Reset), .en(Enable));  // open: Qn, preset
  // Probe on t_ff_1_q
  T_Flip_Flop #(.trigger("falling")) t_ff_4 (
    .clk(t_ff_1_q[2]), .T(1'b1), .Q(t_ff_1_q[3]), .reset(Reset), .en(Enable));  // open: Qn, preset

  // Notes on the sheet:
  //   4 bit up counter
endmodule
