// Logisim project decoder.circ as structural Verilog: 1 circuit, main circuit main
module main (
  input  A__LSB,
  input  B,
  input  C,
  input  D__MSB,
  input  Enable,
  output _0,
  output _1,
  output _2,
  output _3,
  output _4,
  output _5,
  output _6,
  output _7,
  output _8,
  output _9,
  output _10,
  output _11,
  output _12,
  output _13,
  output _14,
  output _15
);

  wire not_1_out, not_2_out, not_3_out, not_4_out;

  not not_1 (not_1_out, A__LSB);
  not not_2 (not_2_out, B);
  not not_3 (not_3_out, C);
  not not_4 (not_4_out, D__MSB);
  and and_1 (_0, Enable, not_4_out, not_3_out, not_2_out, not_1_out);
  and and_2 (_1, Enable, not_4_out, not_3_out, not_2_out, A__LSB);
  and and_3 (_2, Enable, not_4_out, not_3_out, B, not_1_out);
  and and_4 (_3, Enable, not_4_out, not_3_out, B, A__LSB);
  and and_5 (_4, Enable, not_4_out, C, not_2_out, not_1_out);
  and and_6 (_6, Enable, not_4_out, C, B, not_1_out);
  and and_7 (_5, Enable, not_4_out, C, not_2_out, A__LSB);
  and and_8 (_7, Enable, not_4_out, C, B, A__LSB);
  and and_9 (_8, Enable, D__MSB, not_3_out, not_2_out, not_1_out);
  and and_10 (_9, Enable, D__MSB, not_3_out, not_2_out, A__LSB);
  and and_11 (_11, Enable, D__MSB, not_3_out, B, A__LSB);
  and and_12 (_10, Enable, D__MSB, not_3_out, B, not_1_out);
  and and_13 (_12, Enable, D__MSB, C, not_2_out, not_1_out);
  and and_14 (_13, Enable, D__MSB, C, not_2_out, A__LSB);
  and and_15 (_14, Enable, D__MSB, C, B, not_1_out);
  and and_16 (_15, Enable, D__MSB, C, B, A__LSB);

  // Notes on the sheet:
  //   4:16 Decoder
endmodule
