// Logisim project input.circ as structural Verilog: 6 circuits, main circuit main
// Runway Status
module main (
  input  Direction_bit_0,
  input  Direction_bit_1,
  input  Enable
);

  wire clock_1_out, Runway_Picker_en_2, Runway_Picker_o1, Runway_Picker_o2, Runway_Picker_o3,
       Runway_Picker_o4, Runway_status_runway_a_feedback, Runway_status_runway_a_status,
       Runway_status_runway_b_feedback, Runway_status_runway_b_status, Runway_status_wait_signal;

  runway_picker Runway_Picker (
    .B(Runway_status_runway_b_feedback), .A(Runway_status_runway_a_feedback), .En(Enable),
    .D1(Direction_bit_1), .D0(Direction_bit_0), .En_2(Runway_Picker_en_2), .O4(Runway_Picker_o4),
    .O3(Runway_Picker_o3), .O2(Runway_Picker_o2), .O1(Runway_Picker_o1));
  runway_status Runway_status (
    .I3(Runway_Picker_o1), .I2(Runway_Picker_o2), .I1(Runway_Picker_o3), .I0(Runway_Picker_o4),
    .Enable(Runway_Picker_en_2), .Clock(clock_1_out), .Runway_B_Feedback(Runway_status_runway_b_feedback),
    .Runway_A_Feedback(Runway_status_runway_a_feedback), .Runway_B_Status(Runway_status_runway_b_status),
    .Runway_A_Status(Runway_status_runway_a_status), .Wait_Signal(Runway_status_wait_signal));
  Clock clock_1 (.out(clock_1_out));
  LED led_1 (.in(Runway_status_wait_signal));
  LED led_2 (.in(Runway_status_wait_signal));
  LED Wait_For_Landing (.in(Runway_status_wait_signal));
  LED led_3 (.in(Runway_status_runway_b_status));
  LED led_4 (.in(Runway_status_runway_a_status));
  LED led_5 (.in(Runway_status_runway_a_status));
  LED led_6 (.in(Runway_status_runway_a_status));
  LED led_7 (.in(Runway_status_runway_a_status));
  LED led_8 (.in(Runway_status_runway_a_status));
  LED led_9 (.in(Runway_status_runway_a_status));
  LED led_10 (.in(Runway_status_runway_a_status));
  LED led_11 (.in(Runway_status_runway_b_status));
  LED led_12 (.in(Runway_status_wait_signal));
  LED led_13 (.in(Runway_status_wait_signal));
  LED Wait_For_Landing_2 (.in(Runway_status_wait_signal));
  LED led_14 (.in(Runway_status_runway_b_status));
  LED led_15 (.in(Runway_status_runway_b_status));
  LED led_16 (.in(Runway_status_runway_b_status));
  LED led_17 (.in(Runway_status_runway_b_status));
  LED led_18 (.in(Runway_status_runway_b_status));

  // Notes on the sheet:
  //   Key for directions:
  //   00 -> East
  //   01 -> North
  //   10 -> West
  //   11 -> South
  //   N
  //   W
  //   S
  //   E
  //   Main circuit
  //   Runway A
  //   Runway B
endmodule

module runway_picker (
  input  B,
  input  A,
  input  En,
  input  D1,
  input  D0,
  output En_2,
  output O4,
  output O3,
  output O2,
  output O1
);

  wire and_1_out, and_2_out, not_1_out, not_2_out, not_3_out, or_1_out;

  and and_1 (and_1_out, B, A);
  not not_1 (not_1_out, B);
  not not_2 (not_2_out, D1);
  and and_2 (and_2_out, not_1_out, not_2_out);
  not not_3 (not_3_out, and_1_out);
  or or_1 (or_1_out, A, and_2_out);
  and and_3 (O4, En, 1'b1);
  and and_4 (O3, En, and_1_out);
  and and_5 (O2, En, not_3_out);
  and and_6 (O1, En, or_1_out);

  assign En_2 = En;

  // Notes on the sheet:
  //   Input format:
  //   D0 signifies direction bit 0
  //   D1 signifies direction bit 1
  //   A signifies if runway A is full or free
  //   B signifies if runway B is full or free
  //   Runway Picker
  //   The circuit assigns a runway based on the direction of travel
  //   O4 = 1
  //   O3 = A.B
  //   O2 = (A.B)'
  //   O1 = A + B'.D2'
  //   Output logic:
endmodule

module runway_status (
  input  I3,
  input  I2,
  input  I1,
  input  I0,
  input  Enable,
  input  Clock,
  output Runway_B_Feedback,
  output Runway_A_Feedback,
  output Runway_B_Status,
  output Runway_A_Status,
  output Wait_Signal
);

  wire _4_16_Decoder__10, _4_16_Decoder__11;

  decoder _4_16_Decoder (
    .A__LSB(I3), .B(I2), .C(I1), .D__MSB(I0), .Enable(Enable), ._10(_4_16_Decoder__10),
    ._11(_4_16_Decoder__11), ._13(Wait_Signal));  // open: _0, _1, _2, _3, _4, _5, _6, _7, _8, _9, _12, _14, _15
  timer Runway_A_Timer (
    .Signal(_4_16_Decoder__10), .Enable(Enable), .Clock(Clock), .Feedback(Runway_A_Feedback),
    .Status(Runway_A_Status));
  timer Runway_B_Timer (
    .Signal(_4_16_Decoder__11), .Enable(Enable), .Clock(Clock), .Feedback(Runway_B_Feedback),
    .Status(Runway_B_Status));

  // Notes on the sheet:
  //   Input explanation:
  //   a
  //   b
  //   d
  //   I0-I3 signify the outputs from Runway Picker circuit
  //   Runway Status
  //   The circuit keeps the designated runway full i.e outputs 1 during the period of landing/take off
  //   Output explanation:
  //   Runway status light up for 15 seconds during landing/take off
  //   Runway feedback holds the value of runway status and acts as input for runway picker during the next input
endmodule

module decoder (
  input  A__LSB,
  input  B,
  input  C,
  input  D__MSB,
  input  Enable,
  output _0,
  output _1,
  output _2,
  output _3,
  output _4,
  output _5,
  output _6,
  output _7,
  output _8,
  output _9,
  output _10,
  output _11,
  output _12,
  output _13,
  output _14,
  output _15
);

  wire not_1_out, not_2_out, not_3_out, not_4_out;

  not not_1 (not_1_out, A__LSB);
  not not_2 (not_2_out, B);
  not not_3 (not_3_out, C);
  not not_4 (not_4_out, D__MSB);
  and and_1 (_1, Enable, not_4_out, not_3_out, not_2_out, A__LSB);
  and and_2 (_0, Enable, not_4_out, not_3_out, not_2_out, not_1_out);
  and and_3 (_2, Enable, not_4_out, not_3_out, B, not_1_out);
  and and_4 (_3, Enable, not_4_out, not_3_out, B, A__LSB);
  and and_5 (_4, Enable, not_4_out, C, not_2_out, not_1_out);
  and and_6 (_5, Enable, not_4_out, C, not_2_out, A__LSB);
  and and_7 (_6, Enable, not_4_out, C, B, not_1_out);
  and and_8 (_7, Enable, not_4_out, C, B, A__LSB);
  and and_9 (_9, Enable, D__MSB, not_3_out, not_2_out, A__LSB);
  and and_10 (_8, Enable, D__MSB, not_3_out, not_2_out, not_1_out);
  and and_11 (_11, Enable, D__MSB, not_3_out, B, A__LSB);
  and and_12 (_10, Enable, D__MSB, not_3_out, B, not_1_out);
  and and_13 (_12, Enable, D__MSB, C, not_2_out, not_1_out);
  and and_14 (_13, Enable, D__MSB, C, not_2_out, A__LSB);
  and and_15 (_14, Enable, D__MSB, C, B, not_1_out);
  and and_16 (_15, Enable, D__MSB, C, B, A__LSB);

  // Notes on the sheet:
  //   4:16 Decoder
  //   A basic decoder designed using logic gates
endmodule

module counter (
  input  Clock,
  input  Reset,
  output Carry_is_1_when_counter_finishes
);

  wire and_1_out, not_1_out;
  wire [3:0] t_ff_1_q;

  and and_1 (and_1_out, not_1_out, Clock);
  not not_1 (not_1_out, Carry_is_1_when_counter_finishes);
  T_Flip_Flop t_ff_1 (.clk(and_1_out), .T(1'b1), .Q(t_ff_1_q[0]), .reset(Reset), .en(1'b1));  // open: Qn, preset
  and and_2 (Carry_is_1_when_counter_finishes, t_ff_1_q[3], t_ff_1_q[2]);
  T_Flip_Flop #(.trigger("falling")) t_ff_2 (
    .clk(t_ff_1_q[0]), .T(1'b1), .Q(t_ff_1_q[1]), .reset(Reset), .en(1'b1));  // open: Qn, preset
  T_Flip_Flop #(.trigger("falling")) t_ff_3 (
    .clk(t_ff_1_q[1]), .T(1'b1), .Q(t_ff_1_q[2]), .reset(Reset), .en(1'b1));  // open: Qn, preset
  // Probe on t_ff_1_q
  T_Flip_Flop #(.trigger("falling")) t_ff_4 (
    .clk(t_ff_1_q[2]), .T(1'b1), .Q(t_ff_1_q[3]), .reset(Reset), .en(1'b1));  // open: Qn, preset

  // Notes on the sheet:
  //   Asynchronous counter circuit that stops counting as soon as it reaches the 0xD
  //   4 bit up counter
endmodule

module timer (
  input  Signal,
  input  Enable,
  input  Clock,
  output Feedback,
  output Status
);

  wire Counter_carry_is_1_when_counter_finishes, not_1_out, not_2_out, s_r_ff_1_q;

  S_R_Flip_Flop s_r_ff_1 (
    .S(Signal), .clk(Clock), .R(1'b0), .Q(s_r_ff_1_q), .reset(Counter_carry_is_1_when_counter_finishes));  // open: Qn, preset, en
  counter Counter (
    .Carry_is_1_when_counter_finishes(Counter_carry_is_1_when_counter_finishes), .Clock(Clock),
    .Reset(not_2_out));
  not not_1 (not_1_out, Counter_carry_is_1_when_counter_finishes);
  not not_2 (not_2_out, s_r_ff_1_q);
  and and_1 (Status, s_r_ff_1_q, not_1_out);
  D_Flip_Flop d_ff_1 (.clk(Enable), .D(Status), .Q(Feedback));  // open: Qn, preset, en, reset

  // Notes on the sheet:
  //   Timer
  //   A circuit that combines the use of flip flop and counter to give feedback
endmodule
