// Logisim project runway_picker.circ as structural Verilog: 1 circuit, main circuit main
module main (
  input  [4:0] D1D2AB,
  output [3:0] O4O3O2O1
);

  wire and_1_out, and_2_out, not_1_out, not_2_out, not_3_out, or_1_out;

  and and_1 (and_1_out, D1D2AB[1], D1D2AB[2]);
  not not_1 (not_1_out, D1D2AB[1]);
  not not_2 (not_2_out, D1D2AB[3]);
  and and_2 (and_2_out, not_1_out, not_2_out);
  not not_3 (not_3_out, and_1_out);
  or or_1 (or_1_out, D1D2AB[2], and_2_out);
  and and_3 (O4O3O2O1[3], D1D2AB[0], 1'b1);
  and and_4 (O4O3O2O1[2], D1D2AB[0], and_1_out);
  and and_5 (O4O3O2O1[1], D1D2AB[0], not_3_out);
  and and_6 (O4O3O2O1[0], D1D2AB[0], or_1_out);

  // Notes on the sheet:
  //   Runway Picker
  //   O4 = 1
  //   O3 = A.B
  //   O2 = (A.B)'
  //   O1 = A + B'.D2'
endmodule
