// Logisim project runway_status.circ as structural Verilog: 1 circuit, main circuit main
module main (
  input  [4:0] Bit_0_is_enable,
  output Runway_B_Status,
  output Runway_A_Status,
  output Wait_signal
);

  wire _4_16_Decoder__10, _4_16_Decoder__11, clock_1_out, clock_2_out, counter_1_carry, counter_2_carry,
       not_1_out, not_2_out, not_3_out, not_4_out, s_r_ff_1_q, s_r_ff_2_q;

  decoder_main _4_16_Decoder (
    .A__LSB(Bit_0_is_enable[1]), .B(Bit_0_is_enable[2]), .C(Bit_0_is_enable[3]), .D__MSB(Bit_0_is_enable[4]),
    .Enable(Bit_0_is_enable[0]), ._10(_4_16_Decoder__10), ._11(_4_16_Decoder__11), ._13(Wait_signal));  // open: _0, _1, _2, _3, _4, _5, _6, _7, _8, _9, _12, _14, _15
  Clock clock_1 (.out(clock_1_out));
  and and_1 (Runway_A_Status, not_1_out, s_r_ff_1_q);
  not not_1 (not_1_out, counter_1_carry);
  S_R_Flip_Flop s_r_ff_1 (
    .S(_4_16_Decoder__10), .clk(clock_1_out), .R(1'b0), .Q(s_r_ff_1_q), .reset(counter_1_carry));  // open: Qn, preset, en
  Counter #(.width(4), .max('hd), .ongoal("stay")) counter_1 (
    .carry(counter_1_carry), .clk(clock_1_out), .clr(not_2_out));  // open: load, D, count, Q
  not not_2 (not_2_out, s_r_ff_1_q);
  Clock clock_2 (.out(clock_2_out));
  and and_2 (Runway_B_Status, not_4_out, s_r_ff_2_q);
  S_R_Flip_Flop s_r_ff_2 (
    .S(_4_16_Decoder__11), .clk(clock_2_out), .R(1'b0), .Q(s_r_ff_2_q), .reset(counter_2_carry));  // open: Qn, preset, en
  Counter #(.width(4), .max('hd), .ongoal("stay")) counter_2 (
    .carry(counter_2_carry), .clk(clock_2_out), .clr(not_3_out));  // open: load, D, count, Q
  not not_3 (not_3_out, s_r_ff_2_q);
  not not_4 (not_4_out, counter_2_carry);

  // Notes on the sheet:
  //   Bit 1-4 is the output from runway picker
  //   a
  //   b
  //   d
endmodule
